# Fritzing sketch com.gotani.sensor (saved by Fritzing 0.9.3b)
breadboards: 1

parts:
  Part1 = Arduino Board Ethernet
  RHT1 = Humidity and Temperature Sensor RHT03
  RHT2 = Humidity and Temperature Sensor RHT03
  U2 = ESP8266 WiFi Module [part_number=ESP8266]  # not connected
  Part2 = Real Time Clock Module - DS1307 RTC Breakout Board
  LCD1 = LCD screen
  LCM1602_IIC1 = LCM1602 IIC [part_number="LCM1602 IIC" chip_label="LCM1602 IIC" package="DIP (Dual Inline) [THT]"]

nets:
  N1: Part1.A4, Part2.SDA, LCM1602_IIC1.SDA
  N2: Part1.A5, Part2.SCL, LCM1602_IIC1.SCL
  N3: Part1.D3_PWM, Part1.D4, RHT2.Data-signal
  VCC: Part1.5V, RHT1.Vcc, RHT2.Vcc, Part2.5V, LCM1602_IIC1.VCC
  GND: Part1.GND, RHT1.GND_2, RHT2.GND_2, Part2.GND, LCM1602_IIC1.GND
  VSS: LCD1.VSS, LCM1602_IIC1.VDD
  N4: LCD1.VDD, LCM1602_IIC1.V0
  N5: LCD1.V0, LCM1602_IIC1.RS
  N6: LCD1.RS, LCM1602_IIC1.RW
  N7: LCD1.R/W, LCM1602_IIC1.E
  N8: LCD1.E, LCM1602_IIC1.D0
  N9: LCD1.DB0, LCM1602_IIC1.D1
  N10: LCD1.DB1, LCM1602_IIC1.D2
  N11: LCD1.DB2, LCM1602_IIC1.D3
  N12: LCD1.DB3, LCM1602_IIC1.D4
  N13: LCD1.DB4, LCM1602_IIC1.D5
  N14: LCD1.DB5, LCM1602_IIC1.D6
  N15: LCD1.DB6, LCM1602_IIC1.D7
  N16: LCD1.DB7, LCM1602_IIC1.A
  N17: LCD1.LED-, LCM1602_IIC1.K

custom parts:
  ESP8266 WiFi Module: Generic WiFi Module based on the ESP8266 with onboard PCB antenna and UART communications
  LCD screen: A standard character display, usually with 2x16 characters. Comes in many colors.
  LCM1602 IIC: I2C-Module to use a 1602 or 2004 LCD on with the wire.h libory Serial LCD Modul
